// Logisim project 1bit_CPU.circ as structural Verilog: 2 circuits, main circuit One_Bit_CPU
module CPU_and_ProgramRom (
);

  wire MasterClock_out, por_1_out;
  wire [7:0] ProgramROM_data;
  wire [11:0] one_bit_cpu_1_instructionaddress;

  Clock #(.highDuration(2), .lowDuration(2)) MasterClock (.out(MasterClock_out));
  POR por_1 (.out(por_1_out));
  ROM #(.addrWidth(12)) ProgramROM (.addr(one_bit_cpu_1_instructionaddress), .data(ProgramROM_data));
  One_Bit_CPU one_bit_cpu_1 (
    .Reset(por_1_out), .Clock(MasterClock_out), .InstructionIn(ProgramROM_data),
    .InstructionAddress(one_bit_cpu_1_instructionaddress));  // open: DataIn, DataOut, Write, DataAddress

  // Notes on the sheet:
  //   contents of ProgramROM (hex, n*v repeats v):
  //   8c 60 f0 5 61 63
endmodule

module One_Bit_CPU (
  input  Reset,
  input  Clock,
  input  DataIn,
  input  [7:0] InstructionIn,
  output DataOut,
  output Write,
  output [10:0] DataAddress,
  output [11:0] InstructionAddress
);

  wire Accumulator_q, bitselector_1_out, Clk2, FetchNext_qn, not_3_out;
  wire [2:0] StackPointer_q;
  wire [3:0] and_1_out;
  wire [6:0] FetchNext_q;
  wire [11:0] InstructionRegister_q, multiplexer_1_out, ProgramStack_dout;
  wire [17:0] Microcode_data;
  wire [31:0] demultiplexer_1_out0, Registers_q;

  not not_1 (Clk2, Clock);
  ROM #(.addrWidth(7), .dataWidth(18)) Microcode (
    .addr({FetchNext_q[6:3], InstructionRegister_q[11:10], FetchNext_q[0]}), .data(Microcode_data));
  Counter #(.max('h7), .width(3)) StackPointer (
    .clr(Reset), .load(Microcode_data[16]), .up(Microcode_data[17]), .count(1'b1), .clk(Clock),
    .Q(StackPointer_q));  // open: D, carry
  // Probe on Microcode_data
  and and_1 (and_1_out[0], and_1_out[3], Accumulator_q);
  or or_1 (and_1_out[1], and_1_out[3], Accumulator_q);
  not not_2 (and_1_out[2], Accumulator_q);
  RAM #(.addrWidth(3), .dataWidth(12)) ProgramStack (
    .addr(StackPointer_q), .we(Microcode_data[14]), .oe(Microcode_data[15]), .din(InstructionAddress),
    .dout(ProgramStack_dout));  // open: clk
  T_Flip_Flop FetchNext (
    .T(Microcode_data[13]), .clk(Clk2), .Q(FetchNext_q[0]), .Qn(FetchNext_qn), .reset(Reset));  // open: preset
  Register #(.width(1)) Accumulator (
    .D(bitselector_1_out), .en(Microcode_data[3]), .clk(Clk2), .Q(Accumulator_q), .clr(Reset));
  BitSelector #(.width(7)) bitselector_1 (
    .in({2'b01, DataIn, and_1_out}), .out(bitselector_1_out), .sel(Microcode_data[2:0]));
  Register ExtraByte (.D(InstructionIn), .en(FetchNext_q[0]), .clk(Clock), .Q(InstructionRegister_q[7:0]), .clr(Reset));
  Register InstructionRegister (
    .D(InstructionIn), .en(FetchNext_qn), .clk(Clock), .Q({FetchNext_q[6:3], InstructionRegister_q[11:8]}),
    .clr(Reset));
  Demultiplexer #(.select(5)) demultiplexer_1 (
    .out0(demultiplexer_1_out0[0]), .out1(demultiplexer_1_out0[1]), .out2(demultiplexer_1_out0[2]),
    .out3(demultiplexer_1_out0[3]), .out4(demultiplexer_1_out0[4]), .out5(demultiplexer_1_out0[5]),
    .out6(demultiplexer_1_out0[6]), .out7(demultiplexer_1_out0[7]), .out8(demultiplexer_1_out0[8]),
    .out9(demultiplexer_1_out0[9]), .out10(demultiplexer_1_out0[10]), .out11(demultiplexer_1_out0[11]),
    .out12(demultiplexer_1_out0[12]), .out13(demultiplexer_1_out0[13]), .out14(demultiplexer_1_out0[14]),
    .out15(demultiplexer_1_out0[15]), .out16(demultiplexer_1_out0[16]), .out17(demultiplexer_1_out0[17]),
    .out18(demultiplexer_1_out0[18]), .out19(demultiplexer_1_out0[19]), .out20(demultiplexer_1_out0[20]),
    .out21(demultiplexer_1_out0[21]), .out22(demultiplexer_1_out0[22]), .out23(demultiplexer_1_out0[23]),
    .out24(demultiplexer_1_out0[24]), .out25(demultiplexer_1_out0[25]), .out26(demultiplexer_1_out0[26]),
    .out27(demultiplexer_1_out0[27]), .out28(demultiplexer_1_out0[28]), .out29(demultiplexer_1_out0[29]),
    .out30(demultiplexer_1_out0[30]), .out31(demultiplexer_1_out0[31]), .in(Accumulator_q),
    .sel({FetchNext_q[3], InstructionRegister_q[11:8]}));
  Multiplexer #(.width(12)) multiplexer_1 (
    .in0(InstructionRegister_q), .in1(ProgramStack_dout), .out(multiplexer_1_out), .sel(Microcode_data[12]));
  Counter #(.max('hfff), .width(12)) ProgramCounter (
    .clr(Reset), .load(Microcode_data[10]), .up(not_3_out), .count(1'b1), .clk(Clk2), .D(multiplexer_1_out),
    .Q(InstructionAddress));  // open: carry
  not not_3 (not_3_out, Microcode_data[11]);
  Register #(.width(32)) Registers (
    .D(demultiplexer_1_out0), .en(Microcode_data[4]), .clk(Clk2), .Q(Registers_q), .clr(Reset));
  Counter #(.max('h7ff), .width(11)) AddressLatch_IncDec (
    .clr(Reset), .load(Microcode_data[8]), .up(Microcode_data[9]), .count(1'b1), .clk(Clk2),
    .D(InstructionRegister_q[10:0]), .Q(DataAddress));  // open: carry
  Multiplexer #(.select(5)) multiplexer_2 (
    .in0(Registers_q[0]), .in1(Registers_q[1]), .in2(Registers_q[2]), .in3(Registers_q[3]),
    .in4(Registers_q[4]), .in5(Registers_q[5]), .in6(Registers_q[6]), .in7(Registers_q[7]),
    .in8(Registers_q[8]), .in9(Registers_q[9]), .in10(Registers_q[10]), .in11(Registers_q[11]),
    .in12(Registers_q[12]), .in13(Registers_q[13]), .in14(Registers_q[14]), .in15(Registers_q[15]),
    .in16(Registers_q[16]), .in17(Registers_q[17]), .in18(Registers_q[18]), .in19(Registers_q[19]),
    .in20(Registers_q[20]), .in21(Registers_q[21]), .in22(Registers_q[22]), .in23(Registers_q[23]),
    .in24(Registers_q[24]), .in25(Registers_q[25]), .in26(Registers_q[26]), .in27(Registers_q[27]),
    .in28(Registers_q[28]), .in29(Registers_q[29]), .in30(Registers_q[30]), .in31(Registers_q[31]),
    .out(and_1_out[3]), .sel({FetchNext_q[3], InstructionRegister_q[11:8]}));
  Register #(.width(1)) DataOutLatch (.D(Accumulator_q), .en(Microcode_data[6]), .clk(Clk2), .Q(DataOut), .clr(Reset));
  Register #(.width(1)) WriteLatch (
    .D(InstructionRegister_q[11]), .en(Microcode_data[7]), .clk(Clk2), .Q(Write), .clr(Reset));

  // Other names for the same wires on the sheet: Clk1 = Clock; Rst = Reset

  // Notes on the sheet:
  //   contents of Microcode (hex, n*v repeats v):
  //   8 0 8 0 8 0 8 0 8 0 8 0 8 0 8 0 9 0 9 0 9 0 9 0 9 0 9 0 9 0 9 0 b 0 b 0 b 0 b 0 b 0 b 0 b 0 b 0 10 0
  //   10 0 10 0 10 0 10 0 10 0 10 0 10 0 a 0 0 0 e 0 d 49*0 2000 2400 2000 2400 2000 2400 2000 2400
endmodule
